# Fritzing sketch Schema (saved by Fritzing 0.9.10b)

parts:
  WeMos_D1_Mini1 = WeMos D1 Mini
  U1 = WS2812_RGB_LED_matrix_1x8
  DHT1 = DHT22 Humidity and Temperature Sensor

nets:
  3V3: WeMos_D1_Mini1.3V3, DHT1.VDD
  N1: WeMos_D1_Mini1.5V, U1.connector1
  N2: WeMos_D1_Mini1.D4, DHT1.DATA
  N3: WeMos_D1_Mini1.G, U1.connector0, DHT1.GND
  N4: WeMos_D1_Mini1.RX, U1.connector2
